// Logisim project Compuertas.circ as structural Verilog: 12 circuits, main circuit NandMH
module NandMH (
  input  in_1,
  input  in_2,
  output out_3
);

  wire nand_1_out;

  nand nand_1 (nand_1_out, in_1, in_2);
  not not_1 (out_3, nand_1_out);
endmodule

module NotMH (
  input  in_1,
  output out_2
);

  nand nand_1 (out_2, in_1, in_1, in_1);
endmodule

module OrMH (
  input  in_1,
  input  in_2,
  output out_3
);

  wire not_1_out, not_2_out;

  not not_1 (not_1_out, in_1);
  not not_2 (not_2_out, in_2);
  nand nand_1 (out_3, not_1_out, not_2_out);
endmodule

module XorMH (
  input  A,
  input  B,
  output Out
);

  wire And1_out, And2_out, not_1_out, not_2_out;

  not not_1 (not_1_out, A);
  not not_2 (not_2_out, B);
  and And1 (And1_out, not_1_out, B);
  and And2 (And2_out, A, not_2_out);
  or Or (Out, And1_out, And2_out);
endmodule

module Multiplexor (
  input  A,
  input  S,
  input  B,
  output Out
);

  wire And_1_out, And_2_out, Not_out;

  not Not (Not_out, S);
  and And_1 (And_1_out, A, Not_out);
  and And_2 (And_2_out, S, B);
  or Or (Out, And_1_out, And_2_out);
endmodule

module Dmux (
  input  Sel,
  input  I,
  output Y0,
  output Y1
);

  wire not_1_out;

  not not_1 (not_1_out, Sel);
  and And1 (Y0, not_1_out, I);
  and And2 (Y1, Sel, I);
endmodule

module Not16 (
  input  [15:0] In,
  output [15:0] Out
);

  assign Out = ~In;  // NOT_Gate not_1, 16 bits wide
endmodule

module And16 (
  input  [15:0] A,
  input  [15:0] B,
  output [15:0] out_3
);

  and And1 (out_3[0], A[0], B[0]);
  and And1_2 (out_3[1], A[1], B[1]);
  and And1_3 (out_3[2], A[2], B[2]);
  and And1_4 (out_3[3], A[3], B[3]);
  and And1_5 (out_3[4], A[4], B[4]);
  and And1_6 (out_3[5], A[5], B[5]);
  and And1_7 (out_3[6], A[6], B[6]);
  and And1_8 (out_3[7], A[7], B[7]);
  and And1_9 (out_3[8], A[8], B[8]);
  and And1_10 (out_3[9], A[9], B[9]);
  and And1_11 (out_3[10], A[10], B[10]);
  and And1_12 (out_3[11], A[11], B[11]);
  and And1_13 (out_3[12], A[12], B[12]);
  and And1_14 (out_3[13], A[13], B[13]);
  and And1_15 (out_3[14], A[14], B[14]);
  and And1_16 (out_3[15], A[15], B[15]);
endmodule

module sumador_parcial (
  input  in_1,
  input  in_2,
  output out_3,
  output out_4
);

  xor xor_1 (out_3, in_1, in_2);
  and and_1 (out_4, in_1, in_2);
endmodule

module sumador_completo (
  input  in_1,
  input  in_2,
  input  in_3,
  output out_4,
  output out_5
);

  wire and_1_out, and_2_out, xor_1_out;

  xor xor_1 (xor_1_out, in_1, in_2);
  and and_1 (and_1_out, in_1, in_2);
  xor xor_2 (out_4, xor_1_out, in_3);
  and and_2 (and_2_out, xor_1_out, in_3);
  or or_1 (out_5, and_1_out, and_2_out);
endmodule

module _1_bit_register (
  input  in,
  input  load,
  output out
);

  wire clock_1_out, multiplexer_1_out;

  Multiplexer #(.enable("false")) multiplexer_1 (.in0(out), .in1(in), .out(multiplexer_1_out), .sel(load));
  Clock clock_1 (.out(clock_1_out));
  D_Flip_Flop d_ff_1 (.clk(clock_1_out), .D(multiplexer_1_out), .Q(out));  // open: Qn, preset, en, reset
endmodule

module Register (
  input  [15:0] In,
  input  in_2,
  output [15:0] out
);

  _1_bit_register u_1_bit_register_1 (.in(In[0]), .load(in_2), .out(out[0]));
  _1_bit_register u_1_bit_register_2 (.in(In[1]), .load(in_2), .out(out[1]));
  _1_bit_register u_1_bit_register_3 (.in(In[2]), .load(in_2), .out(out[2]));
  _1_bit_register u_1_bit_register_4 (.in(In[3]), .load(in_2), .out(out[3]));
  _1_bit_register u_1_bit_register_5 (.in(In[4]), .load(in_2), .out(out[4]));
  _1_bit_register u_1_bit_register_6 (.in(In[5]), .load(in_2), .out(out[5]));
  _1_bit_register u_1_bit_register_7 (.in(In[6]), .load(in_2), .out(out[6]));
  _1_bit_register u_1_bit_register_8 (.in(In[7]), .load(in_2), .out(out[7]));
  _1_bit_register u_1_bit_register_9 (.in(In[8]), .load(in_2), .out(out[8]));
  _1_bit_register u_1_bit_register_10 (.in(In[9]), .load(in_2), .out(out[9]));
  _1_bit_register u_1_bit_register_11 (.in(In[10]), .load(in_2), .out(out[10]));
  _1_bit_register u_1_bit_register_12 (.in(In[11]), .load(in_2), .out(out[11]));
  _1_bit_register u_1_bit_register_13 (.in(In[12]), .load(in_2), .out(out[12]));
  _1_bit_register u_1_bit_register_14 (.in(In[13]), .load(in_2), .out(out[13]));
  _1_bit_register u_1_bit_register_15 (.in(In[14]), .load(in_2), .out(out[14]));
  _1_bit_register u_1_bit_register_16 (.in(In[15]), .load(in_2), .out(out[15]));
endmodule
